// Digital circuit Acumulator.dig as structural Verilog
module Acumulator (
  input  NLa,
  input  Ea,
  input  Clk,
  input  I0,
  input  I1,
  input  I2,
  input  I3,
  input  I4,
  input  I5,
  input  I6,
  input  I7,
  output S0,
  output S1,
  output S2,
  output S3,
  output S4,
  output S5,
  output S6,
  output S7
);

  wire not_1_out;

  not not_1 (not_1_out, NLa);
  // Register register_1: pin names not known; wires that end beside it: Clk, Ea, I0, not_1_out, 1'b0, I1, I2, I3, I4, I5, I6, I7, S0, S1, S2, S3, S4, S5, S6, S7
endmodule
